# Fritzing sketch CFESPRelay (saved by Fritzing 0.8.7b)

parts:
  KY-1 = Keyes Relay [package=THT]
  Part1 = FTDI Basic Programmer
  U1 = ESP8266 ESP-01 Upgraded WiFi Module [part_number=ESP8266]
  Power_plug1 = Power plug
  M1 = DC Motor

nets:
  N1: KY-1.signal, U1.GPIO_0
  N2: KY-1.power, Part1.POWER, U1.VCC, U1.CH_PD
  GND: KY-1.ground, Part1.GND, U1.GND
  N3: KY-1.C, M1.pin_2
  N4: KY-1.NO, Power_plug1.VCC
  N5: Part1.RXI, U1.TXD
  N6: Part1.TXO, U1.RXD
  N7: Power_plug1.GND, M1.pin_1

custom parts:
  Keyes Relay: The Keyes 5V relay module is suitable for SCM development, home appliance control. It uses a 5V~12V TIL control signal which can control DC / AC signal.
  ESP8266 ESP-01 Upgraded WiFi Module: Upgraded Version ESP-01,all Flash are upgraded to 1M byte.Also support Cloud service remote transmission.
